// Logisim project reg_file_4x4.circ as structural Verilog: 1 circuit, main circuit main
module main (
  input  [31:0] data_in,
  input  write_enable,
  input  reset,
  output [31:0] data_out
);

  wire clk_out;

  Register #(.width(32)) register_1 (.D(data_in), .en(write_enable), .Q(data_out), .clk(clk_out), .clr(reset));
  Clock clk (.out(clk_out));
endmodule
